// Logisim project NAND.circ as structural Verilog: 1 circuit, main circuit main
module main (
  input  in_1,
  input  in_2,
  input  in_3,
  input  in_4,
  input  in_5,
  input  in_6,
  output AND,
  output out_8,
  output OR,
  output XOR
);

  wire nand_1_out, nand_3_out, nand_4_out, nand_5_out, nand_8_out, nand_9_out;

  nand nand_1 (nand_1_out, in_1, in_1);
  nand nand_2 (out_8, in_2, in_2);
  nand nand_3 (nand_3_out, in_3, in_3);
  nand nand_4 (nand_4_out, in_4, in_4);
  nand nand_5 (nand_5_out, in_5, in_6);
  not nand_6 (AND, nand_1_out);  // NAND_Gate
  nand nand_7 (OR, nand_3_out, nand_4_out);
  nand nand_8 (nand_8_out, in_5, nand_5_out, nand_5_out);
  nand nand_9 (nand_9_out, nand_5_out, in_6);
  nand nand_10 (XOR, nand_8_out, nand_9_out);

  // Notes on the sheet:
  //   NOT
endmodule
