// Logisim project Practica7.circ as structural Verilog: 1 circuit, main circuit main
module main (
  input  X,
  input  X_2,
  input  Z,
  input  Z_2,
  input  Y,
  input  Y_2,
  input  X_3,
  input  X_4,
  input  Z_3,
  input  Z_4,
  input  Y_3,
  input  X_5,
  input  Y_4,
  input  X_6,
  input  Z_5,
  input  Z_6,
  input  Y_5,
  input  X_7,
  input  X_8,
  input  Z_7,
  input  Z_8,
  input  Y_6,
  input  Y_7,
  output out_24,
  output out_25,
  output out_26,
  output out_27,
  output out_28,
  output out_29,
  output out_30,
  output out_31
);

  wire and_1_out, and_2_out, and_3_out, and_4_out, and_5_out, and_6_out, and_7_out, and_8_out, and_9_out,
       and_10_out, and_11_out, and_12_out, and_15_out, and_18_out, not_1_out, not_2_out, not_3_out,
       not_4_out, not_5_out, not_6_out, not_7_out, not_8_out, not_9_out, not_10_out, not_11_out, or_1_out,
       or_2_out, or_3_out, or_7_out, or_8_out;

  not not_1 (not_1_out, Z_3);
  or or_1 (or_1_out, X_6, Z_6);
  and and_1 (and_1_out, X_7, Z_7);
  not not_2 (not_2_out, X_7);
  not not_3 (not_3_out, Z_7);
  not not_4 (not_4_out, Y_6);
  and and_2 (and_2_out, X, Z);
  not not_5 (not_5_out, Y);
  and and_3 (and_3_out, X_3, not_1_out);
  not not_6 (not_6_out, Z_6);
  not not_7 (not_7_out, X_6);
  or or_2 (or_2_out, or_1_out, Y_5);
  and and_4 (and_4_out, and_1_out, Y_6);
  and and_5 (and_5_out, not_2_out, not_3_out);
  and and_6 (and_6_out, not_4_out, X_7);
  and and_7 (and_7_out, and_2_out, Y);
  and and_8 (and_8_out, and_2_out, not_5_out);
  and and_9 (and_9_out, and_3_out, Y_3);
  not not_8 (not_8_out, Y_3);
  or or_3 (or_3_out, not_6_out, not_7_out);
  and and_10 (and_10_out, and_5_out, and_6_out);
  and and_11 (and_11_out, and_3_out, not_8_out);
  and and_12 (and_12_out, or_3_out, or_2_out);
  or or_4 (out_30, and_4_out, and_10_out);
  or or_5 (out_25, and_7_out, and_8_out);
  and and_13 (out_28, not_6_out, and_12_out);
  or or_6 (out_27, and_9_out, and_11_out);
  and and_14 (out_24, X_2, Z_2);
  and and_15 (and_15_out, X_8, Z_8);
  not not_9 (not_9_out, Z_4);
  not not_10 (not_10_out, X_5);
  not not_11 (not_11_out, Z_5);
  and and_16 (out_31, and_15_out, Y_7);
  and and_17 (out_26, X_4, not_9_out);
  and and_18 (and_18_out, not_10_out, Y_4);
  or or_7 (or_7_out, X_5, and_18_out);
  or or_8 (or_8_out, or_7_out, Y_4);
  and and_19 (out_29, or_8_out, not_11_out);
endmodule
