// Logisim project operaciones.circ as structural Verilog: 1 circuit, main circuit main
module main (
  input  in_1,
  input  in_2,
  input  in_3,
  input  in_4,
  input  in_5,
  output out_6,
  output out_7,
  output out_8,
  output out_9
);

  wire and_1_out, and_2_out, nand_1_out, nand_2_out, nand_3_out, xor_1_out;

  xor xor_1 (xor_1_out, in_3, in_4);
  and and_1 (and_1_out, in_3, in_4);
  nand nand_1 (nand_1_out, in_1, in_2);
  nand nand_2 (nand_2_out, in_1, nand_1_out, nand_1_out);
  nand nand_3 (nand_3_out, nand_1_out, in_2);
  xor xor_2 (out_8, xor_1_out, in_5);
  and and_2 (and_2_out, in_5, xor_1_out);
  nand nand_4 (out_6, nand_2_out, nand_3_out);
  and and_3 (out_7, in_1, in_2);
  or or_1 (out_9, and_2_out, and_1_out);

  // Notes on the sheet:
  //   Sumador
  //   SemiSumador
endmodule
